# Fritzing sketch RGB electric imp agent (saved by Fritzing 0.8.3b)
breadboards: 1

parts:
  Part1 = Electric Imp Breakout
  R1 = Resistor [tolerance=±5% resistance=330 package=THT]
  LED1 = RGB LED (com. cathode, rbg) [package="5 mm [THT]"]
  R2 = Resistor [tolerance=±5% resistance=330 package=THT]
  R3 = Resistor [tolerance=±5% resistance=330 package=THT]

nets:
  N1: Part1.2, R1.Pin_0
  N2: Part1.3, R2.Pin_0
  N3: Part1.4, R3.Pin_0
  N4: Part1.9, LED1.common_cathode
  N5: Part1.13, Part1.14
  N6: R1.Pin_1, LED1.green_anode
  N7: LED1.red_anode, R3.Pin_1
  N8: LED1.blue_anode, R2.Pin_1

custom parts:
  Electric Imp Breakout: Electric Imp Breakout Board with onboard 3.3V regulated power supply
